# Fritzing sketch schematics (saved by Fritzing 0.9.2b)
breadboards: 2

parts:
  U1 = MAX7219 [package=dil24]
  Part1 = Arduino Uno (Rev3) - ICSP
  R1 = Resistor [tolerance=±5% resistance=220 package="2010 [SMD]"]
  R2 = Resistor [tolerance=±5% resistance=220 package="2010 [SMD]"]
  R3 = Resistor [tolerance=±5% resistance=220 package="2010 [SMD]"]
  R4 = Resistor [tolerance=±5% resistance=220 package="2010 [SMD]"]
  R5 = Resistor [tolerance=±5% resistance=220 package="2010 [SMD]"]
  R6 = Resistor [tolerance=±5% resistance=220 package="2010 [SMD]"]
  R7 = Resistor [tolerance=±5% resistance=220 package="2010 [SMD]"]
  R8 = Resistor [tolerance=±5% resistance=220 package="2010 [SMD]"]
  R9 = Resistor [tolerance=±5% resistance=220 package=THT]
  LCD1 = LCD screen  # not connected
  S1 = Pushbutton [package="[THT]"]
  R10 = Resistor [tolerance=±5% resistance=220 package=THT]

nets:
  N1: U1.DIN, Part1.D10_PWM/SS
  GND: U1.GND, U1.GND2, Part1.GND, R10.Pin_1
  N2: U1.LOAD, Part1.D8
  N3: U1.CLK, Part1.D9_PWM
  N4: U1.SEGA, R6.Pin_0
  N5: U1.SEGF, R3.Pin_0
  N6: U1.SEGB, R7.Pin_0
  N7: U1.SEGG, R4.Pin_0
  N8: U1.ISET, R9.Pin_1
  VCC: U1.VCC, Part1.D13/SCK, Part1.5V, R9.Pin_0, S1.Pin_1, S1.Pin_2, S1.Pin_3, S1.Pin_4, R10.Pin_0
  N9: U1.SEGC, R8.Pin_0
  N10: U1.SEGE, R2.Pin_0
  N11: U1.SEGDP, R5.Pin_0
  N12: U1.SEGD, R1.Pin_0
